// Digital circuit digital_bitbakery.dig as structural Verilog
module digital_bitbakery (
  input  _1kHz,
  input  [1:0] MiniGame,
  input  Dificuldade,
  output [1:0] MiniGameOut,
  output [3:0] EstadoOut,
  output [2:0] \Pontuação ,
  output db_clock,
  output db_iniciar,
  output [6:0] db_jogada,
  output [1:0] db_minigame,
  output [6:0] db_estado
);

  wire Iniciar_out, Reset_out;
  wire [2:0] u_bitbakery_leds_out;
  wire [6:0] B0_out, u_bitbakery_jogada_out;

  Button B0 (.out(B0_out[0]));
  Button B1 (.out(B0_out[1]));
  Button B2 (.out(B0_out[2]));
  Button B3 (.out(B0_out[3]));
  Button B4 (.out(B0_out[4]));
  Button B5 (.out(B0_out[5]));
  Button B6 (.out(B0_out[6]));
  Button Reset (.out(Reset_out));
  Button Iniciar (.out(Iniciar_out));
  bitbakery #(.applicationType("IVERILOG"), .CodeFile("/home/thaylor/Poli/BitBakery/verilog/simulacao/digital_verilog.v")) u_bitbakery (
    .clock(_1kHz), .reset_in(Reset_out), .iniciar_in(Iniciar_out), .dificuldade(Dificuldade),
    .minigame(MiniGame), .botoes_in(B0_out), .minigame_out(MiniGameOut), .leds_out(u_bitbakery_leds_out),
    .estado_out(EstadoOut), .jogada_out(u_bitbakery_jogada_out), .pontuacao_out(\Pontuação ),
    .db_estado(db_estado), .db_minigame(db_minigame), .db_jogada(db_jogada), .db_iniciar(db_iniciar),
    .db_clock(db_clock));
  LED led_1 (.in(u_bitbakery_leds_out[0]));
  LED led_2 (.in(u_bitbakery_leds_out[1]));
  LED led_3 (.in(u_bitbakery_leds_out[2]));
  LED L0 (.in(u_bitbakery_jogada_out[0]));
  LED L1 (.in(u_bitbakery_jogada_out[1]));
  LED L2 (.in(u_bitbakery_jogada_out[2]));
  LED L3 (.in(u_bitbakery_jogada_out[3]));
  LED L4 (.in(u_bitbakery_jogada_out[4]));
  LED L5 (.in(u_bitbakery_jogada_out[5]));
  LED L6 (.in(u_bitbakery_jogada_out[6]));

  // Notes on the sheet:
  //   _1kHz: Hz: 1000
endmodule
